# Fritzing sketch arduino_ibus_connection (saved by Fritzing 0.9.2b)
breadboards: 1

parts:
  R1 = Resistor [tolerance=±5% resistance=5.6k package=THT]
  IC1 = IC, DIP package, 8 pins [chip_label=MCP2025]
  JP1 = Header 3 [package=molex-1x3_lock]
  Pro_Micro1 = Pro Micro
  JP2 = Header 2 [package=molex-1x2_lock]
  R2 = Resistor [tolerance=±5% resistance=10k package=THT]

nets:
  N1: R1.Pin_0, Pro_Micro1.D10
  N2: R1.Pin_1, JP2.1
  N3: IC1.pin1, JP1.2
  N4: IC1.pin2, Pro_Micro1.D2
  GND: IC1.pin3, JP1.3, Pro_Micro1.GND, JP2.2, R2.Pin_1
  N5: IC1.pin4, JP1.1
  N6: IC1.pin5, Pro_Micro1.D5
  N7: IC1.pin6, Pro_Micro1.D6
  N8: IC1.pin7, R2.Pin_0
  N9: IC1.pin8, Pro_Micro1.VCC

custom parts:
  Pro Micro: The SparkFun Pro Micro is a complete USB-based microcontoller development system, in a very small footprint, capable of implementing many types of projects. All programming can be done via the USB port.
